// Digital circuit UTS_1_15.dig as structural Verilog
module UTS_1_15 (
  input  a,
  input  b,
  input  c,
  input  d
);

  wire and_1_out, and_2_out, and_3_out, and_4_out, or_1_out;

  and and_1 (and_1_out, a, b, ~c);  // And
  and and_2 (and_2_out, ~c, d);  // And
  and and_3 (and_3_out, ~a, c, ~d);  // And
  and and_4 (and_4_out, ~b, c, ~d);  // And
  or or_1 (or_1_out, and_1_out, and_2_out, and_3_out, and_4_out);
  LED X (.in(or_1_out));

  // Notes on the sheet:
  //   UTS RANGKAIAN DIGITAL
  //   15. abc' + c'd + a'cd' + b'cd'
  //   MUJAHID LATIMAHASIN
endmodule
