// Digital circuit UTS_1_2.dig as structural Verilog
module UTS_1_2 (
  input  A,
  input  B,
  input  C,
  input  D
);

  wire and_1_out, and_2_out, and_3_out, and_4_out, and_5_out, and_6_out, or_1_out;

  and and_1 (and_1_out, ~A, ~B, C);  // And
  and and_2 (and_2_out, ~A, C, D);  // And
  and and_3 (and_3_out, ~A, ~C, ~D);  // And
  and and_4 (and_4_out, ~A, B, D);  // And
  and and_5 (and_5_out, A, B, C);
  and and_6 (and_6_out, A, ~B, C);  // And
  or or_1 (or_1_out, and_1_out, and_2_out, and_3_out, and_4_out, and_5_out, and_6_out);
  LED X (.in(or_1_out));

  // Notes on the sheet:
  //   UTS RANGKAIAN DIGITAL
  //   2. A'B'C + A'CD + A'C'D' + A'BD + ABC + AB'C
  //   MUJAHID LATIMAHASIN
endmodule
