// Digital circuit UTS_1_3.dig as structural Verilog
module UTS_1_3 (
  input  X,
  input  Y,
  input  Z
);

  wire and_1_out, and_2_out, and_3_out, or_1_out;

  and and_1 (and_1_out, ~X, ~Y, ~Z);  // And
  and and_2 (and_2_out, Y, ~Z);  // And
  and and_3 (and_3_out, Y, X);
  or or_1 (or_1_out, and_1_out, and_2_out, and_3_out);
  LED A (.in(or_1_out));

  // Notes on the sheet:
  //   X'Y'Z'+YZ'+XY
endmodule
