// Digital circuit UTS_1_8.dig as structural Verilog
module UTS_1_8 (
  input  A,
  input  B,
  input  C,
  input  D
);

  wire and_1_out, and_2_out, and_3_out, and_4_out, and_5_out, or_1_out;

  and and_1 (and_1_out, ~A, B, ~D);  // And
  and and_2 (and_2_out, B, D, C);
  and and_3 (and_3_out, A, B, ~C);  // And
  and and_4 (and_4_out, B, D);
  and and_5 (and_5_out, A, B, C);
  or or_1 (or_1_out, and_1_out, and_2_out, and_3_out, and_4_out, and_5_out);
  LED X (.in(or_1_out));

  // Notes on the sheet:
  //   8. A'BD' + BDC + ABC' + BD + ABC
endmodule
